# Fritzing sketch ultrasonic-radar (saved by Fritzing 0.9.4)
breadboards: 1

parts:
  Part1 = Arduino Uno (Rev3)
  hc-sr1 = hc-sr04
  Nokia_5110_LCD_Module1 = Nokia 5110 LCD
  J1 = Basic Servo

nets:
  N1: Part1.A2, hc-sr1.Trig
  N2: Part1.A3, hc-sr1.Echo
  N3: Part1.D9_PWM, J1.pulse
  N4: Part1.D3_PWM, Nokia_5110_LCD_Module1.VCC, Nokia_5110_LCD_Module1.VCC_(out)
  N5: Part1.D4, Nokia_5110_LCD_Module1.GND, Nokia_5110_LCD_Module1.GND_(out)
  N6: Part1.D5_PWM, Nokia_5110_LCD_Module1.SCE, Nokia_5110_LCD_Module1.SCE_(out)
  N7: Part1.D6_PWM, Nokia_5110_LCD_Module1.RST, Nokia_5110_LCD_Module1.RST_(out)
  N8: Part1.D7, Nokia_5110_LCD_Module1.D/C, Nokia_5110_LCD_Module1.D/C_(out)
  VCC: Part1.5V, hc-sr1.VCC, Nokia_5110_LCD_Module1.DN(MOSI), Nokia_5110_LCD_Module1.DN(MODI)_(out), J1.vcc
  GND: Part1.GND, hc-sr1.GND, Nokia_5110_LCD_Module1.SCLK, Nokia_5110_LCD_Module1.SCLK_(out), Nokia_5110_LCD_Module1.LED_(out), J1.gnd

custom parts:
  Nokia 5110 LCD: Nokia 5110 Graphic 84*48 LCD module such as the Sparkfun LCD-10168 or the clones from Ebay. There is example code for the Arduino available from the Sparkfun site in https://learn.sparkfun.com/tutorials/graphic-lcd-hookup-guide This is a 3.3V device, if you are running it from a 5V micro you need a 5V tolorant level translator such as the 74ahc367 to protect the signal imputs. Rafa G. did a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
